// Logisim project adder_and_subtractor.circ as structural Verilog: 1 circuit, main circuit main
module main (
  input  in_1,
  output [3:0] out_2,
  output [1:0] out_3,
  output out_4,
  output [1:0] out_5,
  output [3:0] out_6,
  output out_7,
  output out_8,
  output [3:0] out_9,
  output out_10
);

  wire subtractor_1_bout;

  Adder #(.width(4)) adder_1 (.a(4'b0010), .b(4'b0100), .out(out_2), .cin(1'b1), .cout(out_4));
  Adder #(.width(4)) adder_2 (.a(4'b1000), .b(4'b1000), .out(out_6), .cin(1'b0), .cout(out_8));
  Adder #(.width(4)) adder_3 (.a(4'b1000), .b(4'b1000), .out(out_9), .cin(1'b1), .cout(out_10));
  Subtractor #(.width(2)) subtractor_1 (.a(2'b00), .b(2'b11), .out(out_3), .bin(in_1), .bout(subtractor_1_bout));
  Subtractor #(.width(2)) subtractor_2 (.a(2'b11), .b(2'b00), .out(out_5), .bin(subtractor_1_bout), .bout(out_7));

  // Notes on the sheet:
  //   1100-0011=1001
  //   lower borrow out tells higher borrow in that lower want borrow 10
  //   higher subtractor will do -1 to the upper number (11 in this example)
  //   and then countinue to calculate. If it need to borrow another 10, it will telles higher borrow in
endmodule
