// Logisim project bit_extender.circ as structural Verilog: 1 circuit, main circuit main
module main (
  output [7:0] out_1,
  output [7:0] out_2,
  output [7:0] out_3,
  output [7:0] out_4,
  output [7:0] out_5,
  output [7:0] out_6
);

  assign out_1 = {{4{1'b0}}, 4'b1010};  // Bit_Extender bit_extender_1
  assign out_2 = {{4{1'b1}}, 4'b1010};  // Bit_Extender bit_extender_2
  assign out_3 = {{4{1'b1}}, 4'b1010};  // Bit_Extender bit_extender_3
  assign out_5 = {{4{1'b1}}, 4'b1010};  // Bit_Extender bit_extender_4
  assign out_6 = {{4{1'b1}}, 4'b1010};  // Bit_Extender bit_extender_5
  assign out_4 = {{4{1'b0}}, 4'b0111};  // Bit_Extender bit_extender_6
endmodule
