// Logisim project question_1109_816.circ as structural Verilog: 1 circuit, main circuit main
module main (
  input  [3:0] in_1,
  output [3:0] out_2,
  output [3:0] out_3
);

  wire [3:0] bit_extender_1_out, negator_1_out, shifter_1_out;

  // Probe on bit_extender_1_out
  assign bit_extender_1_out = {{2{1'b1}}, 2'b10};  // Bit_Extender bit_extender_1
  Shifter #(.width(4), .shift("ar")) shifter_1 (.in(in_1), .\dist (2'b10), .out(shifter_1_out));
  // Probe on shifter_1_out
  Negator #(.width(4)) negator_1 (.in(bit_extender_1_out), .out(negator_1_out));
  // Probe on negator_1_out
  assign out_2 = negator_1_out ^ shifter_1_out;  // Odd_Parity odd_parity_1, 4 bits wide
  assign out_3 = negator_1_out ^ shifter_1_out;  // XOR_Gate xor_1, 4 bits wide
endmodule
