// Logisim project question_1109_817.circ as structural Verilog: 1 circuit, main circuit main
module main (
  output [3:0] out_1,
  output [3:0] out_2
);

  wire bitfinder_1_found, bitfinder_2_found;
  wire [2:0] bitfinder_1_index, bitfinder_2_index;
  wire [3:0] adder_1_out, adder_2_out, bit_extender_1_out, bit_extender_2_out, bit_extender_3_out,
       bit_extender_4_out;

  BitFinder #(.\type ("high1")) bitfinder_1 (.in(8'h8), .index(bitfinder_1_index), .found(bitfinder_1_found));
  BitFinder bitfinder_2 (.in(8'h8), .index(bitfinder_2_index), .found(bitfinder_2_found));
  assign bit_extender_1_out = {{1{1'b0}}, bitfinder_1_index};  // Bit_Extender bit_extender_1
  assign bit_extender_2_out = {{3{1'b0}}, bitfinder_1_found};  // Bit_Extender bit_extender_2
  assign bit_extender_3_out = {{1{1'b0}}, bitfinder_2_index};  // Bit_Extender bit_extender_3
  assign bit_extender_4_out = {{3{1'b0}}, bitfinder_2_found};  // Bit_Extender bit_extender_4
  Adder #(.width(4)) adder_1 (.a(bit_extender_1_out), .b(bit_extender_2_out), .out(adder_1_out));  // open: cin, cout
  Adder #(.width(4)) adder_2 (.a(bit_extender_3_out), .b(bit_extender_4_out), .out(adder_2_out));  // open: cin, cout
  Subtractor #(.width(4)) subtractor_1 (.a(4'b1000), .b(adder_1_out), .out(out_1));  // open: bin, bout
  Subtractor #(.width(4)) subtractor_2 (.a(4'b1000), .b(adder_2_out), .out(out_2));  // open: bin, bout
endmodule
