// Logisim project question_1109_818.circ as structural Verilog: 1 circuit, main circuit main
module main (
  output out_1,
  output out_2
);

  wire bitselector_1_out, bitselector_2_out;
  wire [3:0] bitadder_1_out, bitadder_2_out;

  BitAdder bitadder_1 (.in0(8'h10), .out(bitadder_1_out));
  BitAdder bitadder_2 (.in0(8'h1), .out(bitadder_2_out));
  BitSelector #(.width(4)) bitselector_1 (.in(bitadder_1_out), .out(bitselector_1_out), .sel(2'b00));
  BitSelector #(.width(4)) bitselector_2 (.in(bitadder_2_out), .out(bitselector_2_out), .sel(2'b00));
  Comparator #(.width(1)) comparator_1 (.a(bitselector_1_out), .b(1'b1), .eq(out_1));  // open: gt, lt
  Comparator #(.width(1)) comparator_2 (.a(bitselector_2_out), .b(1'b1), .eq(out_2));  // open: gt, lt
endmodule
