// Logisim project splitter.circ as structural Verilog: 1 circuit, main circuit main
module main (
  input  [7:0] in_1,
  input  in_2,
  input  in_3,
  output [7:0] out_4
);

  // Probe on in_1[6]
  // Probe on {in_3, in_2, in_3, in_2, in_3, in_2, in_3, in_2}
  _7_Segment_Display u_7_segment_display_1 (
    .g(in_1[0]), .f(in_1[1]), .a(in_1[2]), .b(in_1[3]), .e(in_1[4]), .d(in_1[5]), .c(in_1[6]), .dp(in_1[7]));

  assign out_4 = {in_3, in_2, in_3, in_2, in_3, in_2, in_3, in_2};
endmodule
