// Logisim project tunnel_and_probe.circ as structural Verilog: 1 circuit, main circuit main
module main (
  input  [31:0] in_1,
  input  in_2,
  output [31:0] out_3,
  output out_4
);

  // Probe on in_1
  // Probe on in_2

  assign out_3 = in_1;
  assign out_4 = in_2;

  // Other names for the same wires on the sheet: Sample[31:0] = in_1; Tunnel = in_2
endmodule
