// Logisim project question_1109_571.circ as structural Verilog: 1 circuit, main circuit main
module main (
  input  [5:0] in_1
);

  wire [2:0] xnor_1_out;

  // Probe on in_1[2:0]
  // Probe on in_1[5:3]
  // Probe on xnor_1_out
  assign xnor_1_out = ~(in_1[2:0] ^ in_1[5:3]);  // XNOR_Gate xnor_1, 3 bits wide
endmodule
