// Logisim project question_1109_573.circ as structural Verilog: 1 circuit, main circuit main
module main (
  input  in_1,
  input  in_2,
  input  in_3,
  input  in_4,
  input  [1:0] in_5
);

  wire decoder_1_out0, decoder_1_out1, decoder_1_out2, decoder_1_out3, multiplexer_1_out;

  Multiplexer #(.select(2), .enable("false")) multiplexer_1 (
    .in0(in_1), .in1(in_2), .in2(in_3), .in3(in_4), .out(multiplexer_1_out), .sel(in_5));
  LED led_1 (.in(multiplexer_1_out));
  Decoder #(.select(2), .enable("false")) decoder_1 (
    .out0(decoder_1_out0), .out1(decoder_1_out1), .out2(decoder_1_out2), .out3(decoder_1_out3), .sel(in_5));
  LED led_2 (.in(decoder_1_out0));
  LED led_3 (.in(decoder_1_out1));
  LED led_4 (.in(decoder_1_out2));
  LED led_5 (.in(decoder_1_out3));
endmodule
