// Logisim project smg_decoder.circ as structural Verilog: 2 circuits, main circuit main
module main (
  input  in_1,
  input  [3:0] in_2
);

  wire judgment_1_outa, judgment_1_outb, judgment_1_outc, judgment_1_outd, judgment_1_oute, judgment_1_outf,
       judgment_1_outg;

  _7_Segment_Display u_7_segment_display_1 (
    .g(judgment_1_outg), .f(judgment_1_outf), .a(judgment_1_outa), .b(judgment_1_outb), .e(judgment_1_oute),
    .d(judgment_1_outd), .c(judgment_1_outc), .dp(in_1));
  judgment judgment_1 (
    .bit0(in_2[0]), .bit1(in_2[1]), .bit2(in_2[2]), .bit3(in_2[3]), .outa(judgment_1_outa),
    .outb(judgment_1_outb), .outc(judgment_1_outc), .outd(judgment_1_outd), .oute(judgment_1_oute),
    .outf(judgment_1_outf), .outg(judgment_1_outg));
endmodule

module judgment (
  input  bit0,
  input  bit1,
  input  bit2,
  input  bit3,
  output outa,
  output outb,
  output outc,
  output outd,
  output oute,
  output outf,
  output outg
);

  wire _3n2n1, and_1_out, and_2_out, and_7_out, and_10_out, and_12_out, and_16_out, n2n1, n2n1n0, n3n1n0,
       n3n2, n3n21, n31, n31n0, n32, n32n1, not_1_out, not_2_out, not_3_out, not_4_out, not_5_out, not_6_out,
       not_7_out, not_8_out, not_9_out, not_10_out, not_11_out, not_12_out, not_13_out, not_14_out,
       not_15_out;

  and and_1 (and_1_out, n3n2, not_1_out);
  not not_1 (not_1_out, bit0);
  and and_2 (and_2_out, n32, bit0);
  not not_2 (not_2_out, bit3);
  and and_3 (n31, not_2_out, bit1);
  and and_4 (_3n2n1, bit3, n2n1);
  or or_1 (outa, and_1_out, and_2_out, n31, _3n2n1);
  not not_3 (not_3_out, bit3);
  not not_4 (not_4_out, bit2);
  not not_5 (not_5_out, bit3);
  not not_6 (not_6_out, bit1);
  not not_7 (not_7_out, bit0);
  not not_8 (not_8_out, bit2);
  not not_9 (not_9_out, bit1);
  and and_5 (n3n2, not_3_out, not_4_out);
  and and_6 (n3n1n0, not_5_out, not_6_out, not_7_out);
  and and_7 (and_7_out, n31, bit0);
  and and_8 (n2n1, not_8_out, not_9_out);
  or or_2 (outb, n3n2, n3n1n0, and_7_out, n2n1);
  not not_10 (not_10_out, bit3);
  and and_9 (n32, not_10_out, bit2);
  and and_10 (and_10_out, n3n2, bit0);
  or or_3 (outc, n32, and_10_out, n2n1);
  not not_11 (not_11_out, bit0);
  not not_12 (not_12_out, bit1);
  not not_13 (not_13_out, bit0);
  and and_11 (n2n1n0, n2n1, not_11_out);
  and and_12 (and_12_out, n32, not_12_out, bit0);
  and and_13 (n3n21, n3n2, bit1);
  and and_14 (n31n0, n31, not_13_out);
  or or_4 (outd, n2n1n0, and_12_out, n3n21, n31n0);
  or or_5 (oute, n2n1n0, n31n0);
  and and_15 (n32n1, n32, not_14_out);
  not not_14 (not_14_out, bit1);
  and and_16 (and_16_out, n32, not_15_out);
  not not_15 (not_15_out, bit0);
  or or_6 (outf, n3n1n0, n32n1, and_16_out, _3n2n1);
  or or_7 (outg, n3n21, n32n1, _3n2n1, n31n0);

  // Other names for the same wires on the sheet: a = outa; b = outb; b0 = bit0; b1 = bit1; b2 = bit2; b3 = bit3;
  //   c = outc; d = outd; e = oute; f = outf; g = outg

  // Notes on the sheet:
  //   For further optimization, decrease NOT gate
  //   A=n3n2n0+n320+n31+3n2n1
  //   B=n3n2+n3n1n0+n310+n2n1
  //   C=n32+n3n20+n2n1
  //   D=n2n1n0+n32n10+n3n21+n31n0
  //   E=n2n1n0+n31n0
  //   F=n3n1n0+n31n1+n32n0+3n2n1
  //   G=n3n21+n32n1+3n2n1+n31n0
endmodule
