// Logisim project moore.circ as structural Verilog: 1 circuit, main circuit main
module main (
  input  TA,
  input  TB,
  input  in_3
);

  wire and_1_out, and_2_out, clock_1_out, decoder_1_out0, decoder_1_out1, decoder_1_out2, decoder_2_out0,
       decoder_2_out1, decoder_2_out2, not_1_out, not_2_out, not_3_out, not_4_out, not_5_out, not_6_out,
       or_1_out, Store0_q, xor_1_out;
  wire [1:0] and_3_out, and_4_out;

  not not_1 (not_1_out, and_3_out[1]);
  and and_1 (and_1_out, not_1_out, not_2_out, not_3_out);
  not not_2 (not_2_out, Store0_q);
  not not_3 (not_3_out, TA);
  and and_2 (and_2_out, and_3_out[1], not_4_out, not_5_out);
  not not_4 (not_4_out, Store0_q);
  not not_5 (not_5_out, TB);
  Clock clock_1 (.out(clock_1_out));
  xor xor_1 (xor_1_out, and_3_out[1], Store0_q);
  or or_1 (or_1_out, and_1_out, and_2_out);
  D_Flip_Flop Store1 (.clk(clock_1_out), .D(xor_1_out), .Q(and_3_out[1]), .reset(in_3));  // open: Qn, preset, en
  D_Flip_Flop Store0 (.clk(clock_1_out), .D(or_1_out), .Q(Store0_q), .reset(in_3));  // open: Qn, preset, en
  not not_6 (not_6_out, and_3_out[1]);
  Decoder #(.select(2), .enable("false")) decoder_1 (
    .out0(decoder_1_out0), .out1(decoder_1_out1), .out2(decoder_1_out2), .sel(and_3_out));  // open: out3
  and and_3 (and_3_out[0], not_6_out, Store0_q);
  Decoder #(.select(2), .enable("false")) decoder_2 (
    .out0(decoder_2_out0), .out1(decoder_2_out1), .out2(decoder_2_out2), .sel(and_4_out));  // open: out3
  not not_7 (and_4_out[1], and_3_out[1]);
  and and_4 (and_4_out[0], and_3_out[1], Store0_q);
  LED led_1 (.in(decoder_1_out0));
  LED led_2 (.in(decoder_1_out1));
  LED led_3 (.in(decoder_1_out2));
  LED led_4 (.in(decoder_2_out0));
  LED led_5 (.in(decoder_2_out1));
  LED led_6 (.in(decoder_2_out2));

  // Notes on the sheet:
  //   LA
  //   LB
endmodule
