// Logisim project question_1109_574.circ as structural Verilog: 1 circuit, main circuit main
module main (
  input  in_1,
  input  in_2,
  input  in_3,
  input  in_4,
  input  in_5,
  input  [3:0] in_6,
  output out_7,
  output out_8,
  output out_9,
  output out_10,
  output out_11
);

  Demultiplexer #(.select(2), .enable("false")) demultiplexer_1 (
    .out0(out_7), .out1(out_8), .out2(out_9), .out3(out_10), .in(in_1), .sel(in_6[1:0]));
  Multiplexer #(.select(2), .enable("false")) multiplexer_1 (
    .in0(in_2), .in1(in_3), .in2(in_4), .in3(in_5), .out(out_11), .sel(in_6[3:2]));
endmodule
