// Logisim project init_circuit.circ as structural Verilog: 1 circuit, main circuit main
module main (
);

  wire clock_1_out, clock_2_out, clock_3_out, comparator_1_eq, d_ff_1_q;
  wire [7:0] and_1_out, bit_extender_1_out, multiplexer_1_out, or_1_out, register_1_q, register_2_q,
       shifter_1_out, shifter_2_out;

  assign and_1_out = bit_extender_1_out & 8'h1;  // AND_Gate and_1, 8 bits wide
  Clock clock_1 (.out(clock_1_out));
  assign or_1_out = and_1_out | shifter_1_out;  // OR_Gate or_1, 8 bits wide
  Clock clock_2 (.out(clock_2_out));
  Multiplexer #(.width(8)) multiplexer_1 (
    .in0(8'h1), .in1(shifter_2_out), .out(multiplexer_1_out), .sel(d_ff_1_q));  // open: en
  Clock clock_3 (.out(clock_3_out));
  D_Flip_Flop d_ff_1 (.clk(clock_1_out), .D(1'b1), .Q(d_ff_1_q));  // open: Qn, preset, en, reset
  Register register_1 (.D(or_1_out), .Q(register_1_q), .clk(clock_2_out));  // open: en, clr
  Register register_2 (.D(multiplexer_1_out), .Q(register_2_q), .clk(clock_3_out));  // open: en, clr
  Comparator comparator_1 (.a({8{1'b0}}), .b(register_1_q), .eq(comparator_1_eq));  // open: gt, lt
  assign bit_extender_1_out = {{7{comparator_1_eq}}, comparator_1_eq};  // Bit_Extender bit_extender_1
  Shifter shifter_1 (.in(register_1_q), .\dist (3'b001), .out(shifter_1_out));
  Shifter shifter_2 (.in(register_2_q), .\dist (3'b001), .out(shifter_2_out));
endmodule
