// Logisim project latch.circ as structural Verilog: 3 circuits, main circuit main
module main (
  input  CLK,
  input  D,
  input  in_3,
  input  CLK_2,
  input  change_Q_to_1,
  input  enable,
  input  change_Q_to_0,
  output out_8,
  output out_9,
  output out_10,
  output out_11,
  output out_12
);

  wire and_1_out, and_2_out, d_latch_1_q, not_1_out, not_2_out;

  not not_1 (not_1_out, CLK);
  D_latch d_latch_1 (.CLK(not_1_out), .D(in_3), .Q(d_latch_1_q));  // open: nQ
  D_latch d_latch_2 (.CLK(CLK), .D(d_latch_1_q), .Q(out_8), .nQ(out_10));
  D_Flip_Flop d_ff_1 (
    .clk(CLK), .D(in_3), .Q(out_11), .Qn(out_12), .preset(change_Q_to_1), .en(enable), .reset(change_Q_to_0));
  not not_2 (not_2_out, CLK_2);
  and and_1 (and_1_out, D, CLK_2);
  or or_1 (out_9, and_1_out, and_2_out);
  and and_2 (and_2_out, not_2_out, out_9);

  // Notes on the sheet:
  //   D Flip-Flop
  //   Asynchronous circuit
  //   Oscillation apparent
endmodule

module SR_latch (
  input  R,
  input  S,
  output Q,
  output nQ
);

  nor nor_1 (Q, R, nQ);
  nor nor_2 (nQ, Q, S);

  // Notes on the sheet:
  //   Q: pull=up
endmodule

module D_latch (
  input  CLK,
  input  D,
  output Q,
  output nQ
);

  wire and_1_out, and_2_out, not_1_out;

  and and_1 (and_1_out, CLK, not_1_out);
  not not_1 (not_1_out, D);
  and and_2 (and_2_out, CLK, D);
  nor nor_1 (Q, and_1_out, nQ);
  nor nor_2 (nQ, Q, and_2_out);

  // Notes on the sheet:
  //   Q: pull=up
endmodule
