// Logisim project mealy.circ as structural Verilog: 1 circuit, main circuit main
module main (
  input  in_1,
  input  in_2,
  output out_3,
  output out_4
);

  wire and_1_out, clock_1_out, d_ff_1_q, d_ff_3_q, not_1_out, not_2_out;

  Clock clock_1 (.out(clock_1_out));
  not not_1 (not_1_out, in_1);
  and and_1 (and_1_out, d_ff_3_q, in_1);
  not not_2 (not_2_out, in_1);
  D_Flip_Flop d_ff_1 (.clk(clock_1_out), .D(not_1_out), .Q(d_ff_1_q), .reset(in_2));  // open: Qn, preset, en
  D_Flip_Flop d_ff_2 (.clk(clock_1_out), .D(and_1_out), .Q(out_4), .reset(in_2));  // open: Qn, preset, en
  D_Flip_Flop d_ff_3 (.clk(clock_1_out), .D(not_2_out), .Q(d_ff_3_q), .reset(in_2));  // open: Qn, preset, en
  and and_2 (out_3, d_ff_1_q, in_1);
endmodule
